// Logisim project decimal_to_hexa_encoder.circ as structural Verilog: 1 circuit, main circuit main
// B2
module main (
  input  D0,
  input  D1,
  input  D2,
  input  D3,
  input  D4,
  input  D5,
  input  D6,
  input  D7,
  input  D8,
  input  D9,
  input  D10,
  input  D11,
  input  D12,
  input  D13,
  input  D14,
  input  D15,
  output H3,
  output H2,
  output H1,
  output H1_2
);

  or or_1 (H3, D8, D9, D10, D11, D12, D13, D14, D15);
  or or_2 (H2, D15, D14, D13, D12, D7, D6, D5, D4);
  or or_3 (H1, D15, D14, D11, D10, D7, D6, D3, D2);
  or or_4 (H1_2, D15, D13, D11, D9, D7, D5, D3, D1);

  // Notes on the sheet:
  //   Decimal to Hexadecimal Coder (ENCODER) circuit
endmodule
