// Logisim project decimal_to_octal_encoder.circ as structural Verilog: 1 circuit, main circuit main
// B2
module main (
  input  D0,
  input  D1,
  input  D2,
  input  D3,
  input  D4,
  input  D5,
  input  D6,
  input  D7,
  output O2,
  output O1,
  output O0
);

  or or_1 (O2, D4, D5, D6, D7);
  or or_2 (O1, D2, D3, D6, D7);
  or or_3 (O0, D1, D3, D5, D7);

  // Notes on the sheet:
  //   Decimal to Octal Coder (ENCODER) circuit
endmodule
