// Logisim project binary_to_decimal.circ as structural Verilog: 1 circuit, main circuit main
// B2
module main (
  input  B1,
  input  B0,
  output D0,
  output D1,
  output D2,
  output D3
);

  wire not_1_out, not_2_out;

  not not_1 (not_1_out, B1);
  not not_2 (not_2_out, B0);
  and and_1 (D0, not_2_out, not_1_out);
  and and_2 (D1, B0, not_1_out);
  and and_3 (D2, B1, not_2_out);
  and and_4 (D3, B0, B1);

  // Notes on the sheet:
  //   Binary to Decimal Code converter circuit
endmodule
