// Logisim project hexadecimal_to_decimal_using_7segment.circ as structural Verilog: 1 circuit, main circuit main
// B2
module main (
  input  H3,
  input  H2,
  input  H1,
  input  H0
);

  wire and_1_out, and_2_out, and_3_out, and_4_out, and_5_out, and_6_out, and_7_out, and_8_out, and_9_out,
       and_10_out, and_11_out, and_12_out, and_13_out, and_14_out, and_15_out, and_16_out, not_1_out,
       not_2_out, not_3_out, not_4_out, or_1_out, or_2_out, or_3_out, or_4_out, or_5_out, or_6_out, or_7_out,
       or_8_out, or_9_out, or_10_out, or_11_out, or_12_out, or_13_out, or_14_out;

  not not_1 (not_1_out, H3);
  not not_2 (not_2_out, H2);
  not not_3 (not_3_out, H1);
  not not_4 (not_4_out, H0);
  and and_1 (and_1_out, not_4_out, not_3_out, not_2_out, not_1_out);
  and and_2 (and_2_out, H0, not_3_out, not_2_out, not_1_out);
  and and_3 (and_3_out, H1, not_4_out, not_2_out, not_1_out);
  and and_4 (and_4_out, H0, H1, not_2_out, not_1_out);
  and and_5 (and_5_out, H2, not_3_out, not_4_out, not_1_out);
  and and_6 (and_6_out, H2, not_3_out, H0, not_1_out);
  and and_7 (and_7_out, H2, H1, not_4_out, not_1_out);
  and and_8 (and_8_out, H0, H1, H2, not_1_out);
  and and_9 (and_9_out, not_4_out, not_3_out, not_2_out, H3);
  and and_10 (and_10_out, H0, not_3_out, not_2_out, H3);
  and and_11 (and_11_out, H1, not_4_out, not_2_out, H3);
  and and_12 (and_12_out, H0, H1, not_2_out, H3);
  and and_13 (and_13_out, H2, not_3_out, not_4_out, H3);
  and and_14 (and_14_out, H2, not_3_out, H0, H3);
  and and_15 (and_15_out, H2, H1, not_4_out, H3);
  and and_16 (and_16_out, H0, H1, H2, H3);
  or or_1 (or_1_out, and_3_out, and_8_out, and_1_out, and_2_out, and_11_out, and_4_out, and_5_out, and_9_out, and_10_out);
  or or_2 (or_2_out, and_1_out, and_5_out, and_6_out, and_7_out, and_9_out, and_10_out);
  or or_3 (or_3_out, and_3_out, and_4_out, and_5_out, and_6_out, and_7_out, and_9_out, and_10_out);
  or or_4 (or_4_out, and_6_out, and_1_out, and_2_out, and_4_out, and_5_out, and_7_out, and_8_out, and_9_out, and_10_out, and_11_out);
  _7_Segment_Display u_7_segment_display_1 (
    .g(or_3_out), .f(or_2_out), .a(or_7_out), .b(or_1_out), .e(or_5_out), .d(or_6_out), .c(or_4_out),
    .dp(1'b0));
  or or_5 (or_5_out, and_1_out, and_3_out, and_7_out, and_9_out);
  or or_6 (or_6_out, and_1_out, and_3_out, and_4_out, and_6_out, and_7_out, and_9_out);
  or or_7 (or_7_out, and_1_out, and_3_out, and_4_out, and_6_out, and_7_out, and_8_out, and_9_out, and_10_out);
  _7_Segment_Display u_7_segment_display_2 (
    .g(or_13_out), .f(or_12_out), .a(or_11_out), .b(or_14_out), .e(or_8_out), .d(or_10_out), .c(or_9_out));  // open: dp
  buf or_8 (or_8_out, and_11_out);  // OR_Gate
  buf or_9 (or_9_out, and_11_out);  // OR_Gate
  buf or_10 (or_10_out, and_11_out);  // OR_Gate
  buf or_11 (or_11_out, and_11_out);  // OR_Gate
  buf or_12 (or_12_out, and_11_out);  // OR_Gate
  // OR_Gate or_13 has open pins: out=or_13_out
  buf or_14 (or_14_out, and_11_out);  // OR_Gate

  // Notes on the sheet:
  //   D0
  //   D1
  //   D2
  //   D3
  //   D4
  //   D5
  //   D6
  //   D7
  //   D8
  //   D9
  //   D10
  //   D11
  //   D12
  //   D13
  //   D14
  //   D15
  //   Hexadecimal to Decimal Code converter with 7 segment display circuit
endmodule
