// Logisim project octal_to_decimal.circ as structural Verilog: 1 circuit, main circuit main
// B2
module main (
  input  O2,
  input  O1,
  input  O0,
  output D0,
  output D1,
  output D2,
  output D3,
  output D4,
  output D5,
  output D6,
  output D7
);

  wire not_1_out, not_2_out, not_3_out;

  not not_1 (not_1_out, O2);
  not not_2 (not_2_out, O1);
  not not_3 (not_3_out, O0);
  and and_1 (D0, not_3_out, not_2_out, not_1_out);
  and and_2 (D1, O0, not_2_out, not_1_out);
  and and_3 (D2, O1, not_3_out, not_1_out);
  and and_4 (D3, O0, O1, not_1_out);
  and and_5 (D4, O2, not_2_out, not_3_out);
  and and_6 (D5, O2, not_2_out, O0);
  and and_7 (D6, O2, O1, not_3_out);
  and and_8 (D7, O0, O1, O2);

  // Notes on the sheet:
  //   Octal to Decimal Code converter circuit
endmodule
